# Fritzing sketch sketch (saved by Fritzing 0.9.3b)
circuit board: 8.46667cm x 5.64444cm
breadboards: 1

parts:
  Part1 = Arduino Mega ADK (Rev3)
  DHT1 = DHT22 Humidity and Temperature Sensor
  R1 = Resistor [tolerance=±5% resistance=10k package=THT]

nets:
  5V: Part1.5V, DHT1.VDD, R1.Pin_0
  GND: Part1.GND, DHT1.GND
  N1: Part1.D2_PWM, DHT1.DATA, R1.Pin_1
